# Fritzing sketch NodeMCU_2Pomp (saved by Fritzing 0.9.3b)
breadboards: 1

parts:
  U1 = LM2596 step down module
  Power_plug1 = Power plug
  U2 = NodeMCU V3.0
  U3 = 2-Channel 5v Relay Shield [package=relay-2ch5v10a]
  S1 = Pushbutton [package="[THT]"]
  LED1 = DUO LED RG [package="5 mm [THT]"]
  LED2 = DUO LED RG [package="5 mm [THT]"]
  WATER_PUMP1 = water pump/motor  # not connected
  WATER_PUMP2 = water pump/motor  # not connected
  R1 = Resistor [tolerance=±5% resistance=220 package="2010 [SMD]"]
  R2 = Resistor [tolerance=±5% resistance=220 package="2010 [SMD]"]
  R3 = Resistor [tolerance=±5% resistance=220 package="2010 [SMD]"]
  R4 = Resistor [tolerance=±5% resistance=220 package="2010 [SMD]"]

nets:
  N1: U1.IN+, Power_plug1.VCC, U3.K1-In, U3.K2-Off
  N2: U1.IN-, U1.OUT-, Power_plug1.GND
  VIN: U1.OUT+, U2.Vin, U3.VCC
  N3: U2.D1, R3.Pin_0
  N4: U2.D2, S1.Pin_3, S1.Pin_4
  N5: U2.D4, R4.Pin_1
  N6: U2.3V3, S1.Pin_1, S1.Pin_2
  N7: U2.GND#6, U2.GND#13, U2.GND#16, U2.GND#33, U3.GND
  N8: U2.D5, U3.IN1
  N9: U2.D6, U3.IN2
  N10: U2.D7, R1.Pin_1
  N11: U2.D8, R2.Pin_0
  N12: U2.GND#41, LED1.common_cathode, LED2.common_cathode
  N13: LED1.red_anode, R3.Pin_1
  N14: LED1.green_anode, R4.Pin_0
  N15: LED2.red_anode, R1.Pin_0
  N16: LED2.green_anode, R2.Pin_1

custom parts:
  LM2596 step down module: LM2596 DC-DC step down power supply module 3 A.
  NodeMCU V3.0: ESP8266 based NodeMCU
  2-Channel 5v Relay Shield: 2 Channel 5v Relay Shield w. 2x SPD-06VDC-SD-C
  water pump/motor: WATER PUMP BY ARDUBLOCKTR
