# Fritzing sketch smartDevice_ (saved by Fritzing 0.9.3b)
breadboards: 1

parts:
  S1 = Pushbutton [package="[THT]"]
  Parça1 = Soil Moisture Sensor
  U1 = NodeMCU V3.0
  R1 = Resistor [tolerance=±5% resistance=10k package="0402 [SMD]"]
  R2 = Resistor [tolerance=±5% resistance=10k package="0402 [SMD]"]
  M1 = DC Motor
  Q1 = NPN-Transistor [package="TO92 [THT]"]
  R3 = Resistor [tolerance=±5% resistance=10k package="0402 [SMD]"]
  LED2 = DUO LED RG [package="5 mm [THT]"]
  R4 = Resistor [tolerance=±5% resistance=10k package="0402 [SMD]"]
  LED3 = DUO LED RG [package="5 mm [THT]"]
  R5 = Resistor [tolerance=±5% resistance=10k package="0402 [SMD]"]
  R6 = Resistor [tolerance=±5% resistance=10k package="0402 [SMD]"]

nets:
  N1: S1.Pin_1, S1.Pin_2, R1.Pin_1
  VCC: S1.Pin_3, S1.Pin_4, Parça1.VCC, U1.D2, U1.3V3, Q1.B, LED3.common_cathode
  N2: Parça1.SIG, U1.A0
  N3: Parça1.GND, U1.GND#6, U1.GND#13, U1.GND#16, U1.GND#33, R1.Pin_0, M1.pin_2, LED2.common_cathode
  N4: U1.D1, R2.Pin_1
  N5: U1.D4, R4.Pin_0
  N6: U1.D6, R3.Pin_1
  N7: U1.D7, R6.Pin_0
  N8: U1.D8, R5.Pin_1
  N9: R2.Pin_0, LED2.red_anode
  N10: M1.pin_1, Q1.E
  N11: Q1.C, R3.Pin_0
  N12: LED2.green_anode, R4.Pin_1
  N13: LED3.red_anode, R5.Pin_0
  N14: LED3.green_anode, R6.Pin_1

custom parts:
  NodeMCU V3.0: ESP8266 based NodeMCU
